# Fritzing sketch Plano Eléctrico Piranómetro (saved by Fritzing 1.0.3b)
breadboards: 1

parts:
  Componente1 = Arduino Uno (Rev3) - ICSP
  M1 = RioRand LM2596
  DRV_1 = DRV 8825 Stepper Motor Carrier, High Current [part_number="DRV 8825"]
  DRV_2 = DRV 8825 Stepper Motor Carrier, High Current [part_number="DRV 8825"]
  U2 = RS485_SP491 [package=soic-14]  # not connected
  M3 = Stepper Motor - Unipolar
  R1 = Photocell (LDR) [power=0.25W dark_resistance_@0.01lx=300kΩ light_resistance_@100lx=400Ω luminance=10lx package=THT]  # not connected
  M2 = Stepper Motor - Unipolar
  R2 = Photocell (LDR) [power=0.25W dark_resistance_@0.01lx=300kΩ light_resistance_@100lx=400Ω luminance=10lx package=THT]  # not connected
  Adafruit_HUZZAH_ESP8266_Breakout1 = Adafruit HUZZAH ESP8266 Breakout [part_number=2471]
  M4 = RioRand LM2596

nets:
  N1: Componente1.D0/RX, Adafruit_HUZZAH_ESP8266_Breakout1.RX
  N2: Componente1.D1/TX, Adafruit_HUZZAH_ESP8266_Breakout1.TX
  N3: Componente1.D2, DRV_1.STEP
  N4: Componente1.D3_PWM, DRV_1.DIRECTION
  N5: Componente1.D4, DRV_2.STEP
  N6: Componente1.D5_PWM, DRV_2.DIRECTION
  N7: Componente1.5V, DRV_1.VOLTAGE_DD, DRV_2.VOLTAGE_DD
  N8: Componente1.GND, DRV_1.GROUND_LOG, DRV_2.GROUND_LOG
  N9: M1.Pin_3, DRV_1.VOLTAGE_ST/_MT, DRV_2.VOLTAGE_ST/_MT
  N10: M1.Pin_4, DRV_1.GROUND_ST/_MT, DRV_2.GROUND_ST/_MT
  N11: DRV_1.RESET, DRV_1.SLEEP
  N12: DRV_1.OUT_2B, M2.C
  N13: DRV_1.OUT_2A, M2.B
  N14: DRV_1.OUT_1A, M2.COMMON_2
  N15: DRV_1.OUT_1B, M2.D
  N16: DRV_2.RESET, DRV_2.SLEEP
  N17: DRV_2.OUT_2B, M3.C
  N18: DRV_2.OUT_2A, M3.B
  N19: DRV_2.OUT_1A, M3.COMMON_2
  N20: DRV_2.OUT_1B, M3.D
  N21: Adafruit_HUZZAH_ESP8266_Breakout1.3V, M4.Pin_3
  N22: Adafruit_HUZZAH_ESP8266_Breakout1.GND, M4.Pin_4
